// Logisim project ppt.circ as structural Verilog: 2 circuits, main circuit main
module main (
  input  A,
  input  B,
  input  C,
  input  D,
  input  E,
  input  F,
  output out_7,
  output out_8,
  output out_9
);

  wire and_1_out, and_2_out, and_3_out, and_4_out, and_5_out, and_6_out, and_7_out, and_8_out, and_9_out;

  and and_1 (and_1_out, A, F);
  and and_2 (and_2_out, B, D);
  and and_3 (and_3_out, C, E);
  and and_4 (and_4_out, C, D);
  and and_5 (and_5_out, A, E);
  and and_6 (and_6_out, B, F);
  and and_7 (and_7_out, A, D);
  and and_8 (and_8_out, B, E);
  and and_9 (and_9_out, C, F);
  or or_1 (out_7, and_1_out, and_2_out, and_3_out);
  or or_2 (out_8, and_4_out, and_5_out, and_6_out);
  or or_3 (out_9, and_7_out, and_8_out, and_9_out);

  // Notes on the sheet:
  //   V1
  //   V2
  //   E
endmodule

module BUNITINHO (
  input  Papel_j1,
  input  Tesoura_j1,
  input  in_3,
  input  Pedra_j2,
  input  Papel_j2,
  input  in_6,
  output Vitoria_j1,
  output Vitoria_j2,
  output Epate
);

  main main_1 (
    .A(Papel_j1), .B(Tesoura_j1), .C(in_3), .D(Pedra_j2), .E(Papel_j2), .F(in_6), .out_7(Vitoria_j1),
    .out_8(Vitoria_j2), .out_9(Epate));

  // Notes on the sheet:
  //   original
  //   Pedra j1
  //   Tesoura j2
  //   original
  //   original
endmodule
